# Fritzing sketch PressureSensor (saved by Fritzing 0.9.4)
breadboards: 1

parts:
  Part1 = Adafruit Circuit Playground Express [part_number="Adafruit #3333"]
  R1 = Resistor [tolerance=±5% resistance=220 package=THT]
  R2 = Resistor [tolerance=±5% resistance=220 package=THT]
  C1 = Electrolytic Capacitor [capacitance=1µF package="100 mil [THT, electrolytic]"]
  Part2 = Adafruit MPRLS Sensor Breakout [part_number=3965]

nets:
  3.3V: Part1.3.3V, R1.Pin_1, R2.Pin_1, C1.+, Part2.VIN
  GND: Part1.GND, C1.-, Part2.GND
  N1: Part1.D3_A4_SCL, R2.Pin_0, Part2.SCL
  N2: Part1.D2_A5_SDA, R1.Pin_0, Part2.SDA

custom parts:
  Adafruit Circuit Playground Express: Circuit Playground Express is the next step towards a perfect introduction to electronics and programming. We've taken the original Circuit Playground Classic and made it even better! Not only did we pack even more sensors in, we also made it even easier to program. You can now start your journey with Microsoft MakeCode block-based or Javascript programming. Then, you can use the same board to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
  Adafruit MPRLS Sensor Breakout: This pressure sensor is special because it comes with a metal port - you can easily attach a tube to it, to measure air pressure inside a close space. In particular we think this would be a great sensor for use with making DIY assistive tech "Sip & Puff" interfaces, or measuring the pressure within a vacuum chamber or other pressurized container. The port is made of stainless steel and is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
